# Fritzing sketch Untitled Sketch (saved by Fritzing 0.9.3b)
breadboards: 1

parts:
  Part1 = Arduino Nano (Rev3.0) (ICSP)
  V1 = DC Power [voltage=5]
  Part2 = NRF24L01+ Breakout Board
  R1 = Resistor [tolerance=±5% resistance=220 package=THT]
  R2 = Resistor [tolerance=±5% resistance=220 package=THT]  # not connected
  Q1 = NPN-Transistor [package="TO92 [THT]"]

nets:
  GND: Part1.GND, V1.V-, Part2.GND, Q1.C
  N1: Part1.D4, R1.Pin_1
  N2: Part1.D9, Part2.CE
  N3: Part1.D10, Part2.CS
  N4: Part1.VIN, V1.V+
  3V3: Part1.3V3, Part2.VCC
  N5: Part1.D13/SCK, Part2.SCK
  N6: Part1.D12/MISO, Part2.MISO
  N7: Part1.D11/MOSI, Part2.MOSI
  N8: R1.Pin_0, Q1.B
